# Fritzing sketch LaspelyArduino-Schematic (saved by Fritzing 0.9.0b)
breadboards: 1

parts:
  µDuino = Arduino Uno (Rev3)
  R1 = Resistor [tolerance=±5% resistance=1M package=THT]
  R2 = Resistor [tolerance=±5% resistance=1M package=THT]
  LETSGO_switch = SWITCH_SPDT [package=kps-1290]
  ON/OFF_switch = SWITCH-SPST-2 [package=switch-spst-vertical]
  R3 = Resistor [tolerance=±5% resistance=1M package=THT]
  IC1 = Voltage Regulator [package=to220-igo]
  VCC1 = Battery block 9V
  S1 = Pushbutton [package=THT]
  S2 = Pushbutton [package=THT]
  U1 = RELAY [package=relay-jzc]
  D1 = Rectifier Diode [part_number=1N4148 package="Melf DO-213 AB [SMD]"]

nets:
  N1: µDuino.D8, U1.COIL1, D1.cathode
  LOAD pour l'afficheur: µDuino.D10_PWM/SS
  CLOCK pour l'afficheur: µDuino.D11_PWM/MOSI
  DATAIN pour l'afficheur: µDuino.D12/MISO
  GND: µDuino.GND, R1.Pin_1, R2.Pin_1, R3.Pin_1, IC1.GND, VCC1.-, S1.leg0, S2.leg0, U1.COIL2, D1.anode
  N2: µDuino.D2, R1.Pin_0
  N3: µDuino.D3_PWM, R2.Pin_0
  N4: µDuino.D4, LETSGO_switch.P
  N5: µDuino.5V, LETSGO_switch.O, IC1.OUT, S1.leg1, S2.leg1
  N6: LETSGO_switch.S, R3.Pin_0
  N7: ON/OFF_switch.O, VCC1.+
  N8: ON/OFF_switch.P, IC1.IN
  vers le GND de la prise JACK: U1.NO
  vers le LEFT de la prise jack: U1.MAIN
